// Logisim project I8080.circ as structural Verilog: 6 circuits, main circuit main
module main (
  input  [7:0] MEMORY_WORD,
  output f0,
  output [3:0] F1,
  output [4:0] F2
);

  wire als_1_carry_borrow, and_1_out, and_2_out, and_3_out, and_4_out, and_5_out, and_6_out, and_7_out,
       and_8_out, and_9_out, and_10_out, and_11_out, and_17_out, clock_1_out, decoder_1_out0, decoder_1_out1,
       decoder_1_out2, decoder_1_out3, decoder_1_out4, decoder_1_out5, decoder_1_out6, decoder_1_out7,
       decoder_2_out1, decoder_2_out2, decoder_2_out5, decoder_2_out6, decoder_2_out7, decoder_2_out8,
       decoder_2_out10, decoder_2_out13, decoder_2_out14, decoder_2_out15, decoder_3_out1, decoder_3_out2,
       decoder_3_out3, decoder_3_out4, decoder_3_out5, decoder_3_out6, decoder_3_out7, decoder_3_out8,
       decoder_3_out9, decoder_3_out10, decoder_3_out11, decoder_3_out12, decoder_3_out13, decoder_3_out14,
       decoder_3_out15, decoder_3_out16, decoder_3_out17, decoder_3_out18, decoder_3_out19, decoder_3_out20,
       decoder_3_out21, decoder_3_out22, decoder_3_out23, decoder_3_out24, decoder_3_out25, decoder_3_out26,
       decoder_3_out27, decoder_3_out28, decoder_3_out29, decoder_4_out2, decoder_4_out3, decoder_4_out4,
       decoder_4_out5, decoder_4_out6, decoder_4_out7, decoder_4_out8, decoder_4_out9, decoder_4_out10,
       decoder_4_out12, F_q3, flag_processor_1_cy, flag_processor_1_p, flag_processor_1_s,
       flag_processor_1_z, multiplexer_12_out, multiplexer_13_out, multiplexer_14_out, multiplexer_15_out,
       multiplexer_16_out, multiplexer_17_out, multiplexer_18_out, multiplexer_19_out, multiplexer_20_out,
       not_1_out, not_2_out, not_3_out, not_4_out, not_5_out, not_6_out, not_7_out, not_8_out, or_1_out,
       or_2_out, or_3_out, or_4_out, or_5_out, or_6_out, or_7_out, or_8_out, or_9_out, or_10_out, or_11_out,
       or_12_out, or_13_out, or_17_out, or_18_out, or_19_out, or_21_out;
  wire [1:0] and_16_out, decoder_2_out3, or_20_out, rom_1_data;
  wire [2:0] adder_1_out, adder_2_out, and_12_out, B_q4, B_q7, multiplexer_1_out, multiplexer_2_out,
       multiplexer_3_out, multiplexer_4_out, multiplexer_5_out, multiplexer_6_out, or_14_out,
       subtractor_1_out, subtractor_2_out;
  wire [3:0] F_q1, or_25_out;
  wire [7:0] AC_q7, als_1_output, C_q7, D_q7, E_q7, H_q7, HL_LOAD_h_2, HL_LOAD_l_2, L_q7, multiplexer_7_out,
       multiplexer_11_out, ram_1_data, TEMP_q7;
  wire [7:6] B_q1;
  wire [8:0] adder_5_out, CAR_q8, mapping_logic_1_output, multiplexer_21_out, rom_1_data_2, SBR_q8;
  wire [11:11] rom_1_data_3;
  wire [15:0] adder_3_out, adder_4_out, multiplexer_8_out, multiplexer_9_out, multiplexer_10_out, PC_q15,
       SP_q15, subtractor_3_out;

  CONTROL_BLOCK control_block_1 (
    .MEMORY_WORD({B_q1, B_q4, B_q7}), .CLOCK(clock_1_out));  // open: Z, CY, P, S, F1, F2, f0
  Multiplexer #(.width(3), .enable("false")) multiplexer_1 (
    .in0(B_q4), .in1(multiplexer_2_out), .out(multiplexer_1_out), .sel(f0));
  Subtractor #(.width(3)) subtractor_1 (.a(B_q4), .b(3'b001), .out(subtractor_1_out));  // open: bin, bout
  Multiplexer #(.width(3), .enable("false")) multiplexer_2 (
    .in0(adder_1_out), .in1(subtractor_1_out), .out(multiplexer_2_out), .sel(B_q4[0]));
  Adder #(.width(3)) adder_1 (.a(3'b001), .b(B_q4), .out(adder_1_out));  // open: cin, cout
  Subtractor #(.width(3)) subtractor_2 (.a(B_q7), .b(3'b001), .out(subtractor_2_out));  // open: bin, bout
  and and_1 (and_1_out, decoder_1_out0, or_1_out);
  or or_1 (or_1_out, decoder_3_out23, decoder_3_out21, decoder_3_out1, decoder_2_out14);
  Adder #(.width(3)) adder_2 (.a(B_q7), .b(3'b001), .out(adder_2_out));  // open: cin, cout
  Decoder #(.select(3), .enable("false")) decoder_1 (
    .out0(decoder_1_out0), .out1(decoder_1_out1), .out2(decoder_1_out2), .out3(decoder_1_out3),
    .out4(decoder_1_out4), .out5(decoder_1_out5), .out6(decoder_1_out6), .out7(decoder_1_out7),
    .sel(multiplexer_5_out));
  and and_2 (and_2_out, decoder_1_out2, or_1_out);
  and and_3 (and_3_out, decoder_1_out1, or_1_out);
  Multiplexer #(.width(3), .enable("false")) multiplexer_3 (
    .in0(B_q7), .in1(multiplexer_4_out), .out(multiplexer_3_out), .sel(f0));
  Multiplexer #(.width(3), .enable("false")) multiplexer_4 (
    .in0(adder_2_out), .in1(subtractor_2_out), .out(multiplexer_4_out), .sel(B_q4[0]));
  Multiplexer #(.width(3), .enable("false")) multiplexer_5 (
    .in0(multiplexer_1_out), .in1(multiplexer_3_out), .out(multiplexer_5_out), .sel(decoder_2_out14));
  and and_4 (and_4_out, decoder_1_out3, or_1_out);
  and and_5 (and_5_out, decoder_1_out5, or_1_out);
  and and_6 (and_6_out, decoder_1_out4, or_1_out);
  Decoder #(.select(4), .enable("false")) decoder_2 (
    .out1(decoder_2_out1), .out2(decoder_2_out2), .out3(decoder_2_out3[0]), .out4(decoder_2_out3[1]),
    .out5(decoder_2_out5), .out6(decoder_2_out6), .out7(decoder_2_out7), .out8(decoder_2_out8),
    .out9(or_20_out[1]), .out10(decoder_2_out10), .out13(decoder_2_out13), .out14(decoder_2_out14),
    .out15(decoder_2_out15), .sel(F1));  // open: out0, out11, out12
  and and_7 (and_7_out, decoder_1_out6, or_1_out);
  and and_8 (and_8_out, decoder_1_out7, or_1_out);
  or or_2 (or_2_out, or_13_out, and_8_out, decoder_2_out10, decoder_3_out29, decoder_2_out7);
  or or_3 (or_3_out, and_5_out, decoder_3_out26, decoder_2_out1, decoder_2_out15);
  or or_4 (or_4_out, and_6_out, decoder_3_out25, decoder_2_out1, decoder_2_out15);
  or or_5 (or_5_out, and_1_out, decoder_3_out16);
  Decoder #(.select(5), .enable("false")) decoder_3 (
    .out1(decoder_3_out1), .out2(decoder_3_out2), .out3(decoder_3_out3), .out4(decoder_3_out4),
    .out5(decoder_3_out5), .out6(decoder_3_out6), .out7(decoder_3_out7), .out8(decoder_3_out8),
    .out9(decoder_3_out9), .out10(decoder_3_out10), .out11(decoder_3_out11), .out12(decoder_3_out12),
    .out13(decoder_3_out13), .out14(decoder_3_out14), .out15(decoder_3_out15), .out16(decoder_3_out16),
    .out17(decoder_3_out17), .out18(decoder_3_out18), .out19(decoder_3_out19), .out20(decoder_3_out20),
    .out21(decoder_3_out21), .out22(decoder_3_out22), .out23(decoder_3_out23), .out24(decoder_3_out24),
    .out25(decoder_3_out25), .out26(decoder_3_out26), .out27(decoder_3_out27), .out28(decoder_3_out28),
    .out29(decoder_3_out29), .sel(F2));  // open: out0, out30, out31
  or or_6 (or_6_out, and_3_out, decoder_3_out17);
  or or_7 (or_7_out, and_7_out, decoder_3_out24);
  or or_8 (or_8_out, and_2_out, decoder_3_out18);
  or or_9 (or_9_out, and_4_out, decoder_3_out19);
  or or_10 (or_10_out, decoder_3_out16, decoder_3_out17, decoder_3_out18, decoder_3_out19, decoder_3_out20, decoder_3_out21);
  or or_11 (or_11_out, decoder_3_out6, decoder_2_out13, decoder_3_out7, decoder_3_out26, decoder_3_out25);
  or or_12 (or_12_out, decoder_3_out26, decoder_3_out23, decoder_3_out17, decoder_3_out18, decoder_3_out19, decoder_3_out6, decoder_2_out13, decoder_3_out16, decoder_3_out7, decoder_3_out20, decoder_3_out21, decoder_3_out24, decoder_3_out25);
  or or_13 (or_13_out, decoder_3_out2, decoder_3_out3, decoder_3_out4, decoder_3_out5, decoder_3_out6, decoder_3_out7, decoder_3_out8, decoder_3_out9, decoder_3_out10, decoder_3_out11, decoder_3_out12, decoder_3_out13, decoder_3_out14, decoder_3_out20, decoder_3_out22, decoder_3_out24);
  and and_9 (and_9_out, multiplexer_1_out[1], or_11_out);
  and and_10 (and_10_out, multiplexer_1_out[0], or_11_out);
  and and_11 (and_11_out, multiplexer_1_out[2], or_11_out);
  or or_14 (or_14_out[0], and_10_out, decoder_3_out24, decoder_3_out23);
  or or_15 (or_14_out[1], and_9_out, decoder_3_out24, decoder_3_out23, or_10_out);
  or or_16 (or_14_out[2], and_11_out, decoder_3_out24, decoder_3_out23, or_10_out);
  Multiplexer #(.width(3), .enable("false")) multiplexer_6 (
    .in0(multiplexer_3_out), .in1(or_14_out), .out(multiplexer_6_out), .sel(or_12_out));
  Multiplexer #(.select(3), .width(8), .enable("false")) multiplexer_7 (
    .in0({B_q1, B_q4, B_q7}), .in1(C_q7), .in2(D_q7), .in3(E_q7), .in4(H_q7), .in5(L_q7), .in6(ram_1_data),
    .in7(AC_q7), .out(multiplexer_7_out), .sel(multiplexer_6_out));
  not not_1 (not_1_out, decoder_2_out15);
  Multiplexer #(.width(16), .enable("false")) multiplexer_8 (
    .in0({H_q7, L_q7}), .in1(SP_q15), .out(multiplexer_8_out), .sel(decoder_2_out6));
  Shift_Register B (
    .shift(1'b0), .clk(clock_1_out), .load(or_5_out), .d0(multiplexer_7_out[7]), .q0(B_q1[7]),
    .d1(multiplexer_7_out[6]), .q1(B_q1[6]), .d2(multiplexer_7_out[5]), .q2(B_q4[2]),
    .d3(multiplexer_7_out[4]), .q3(B_q4[1]), .d4(multiplexer_7_out[3]), .q4(B_q4[0]),
    .d5(multiplexer_7_out[2]), .q5(B_q7[2]), .d6(multiplexer_7_out[1]), .q6(B_q7[1]),
    .d7(multiplexer_7_out[0]), .q7(B_q7[0]));  // open: in, out, clr
  Shift_Register D (
    .shift(1'b0), .clk(clock_1_out), .load(or_8_out), .d0(multiplexer_7_out[7]), .q0(D_q7[7]),
    .d1(multiplexer_7_out[6]), .q1(D_q7[6]), .d2(multiplexer_7_out[5]), .q2(D_q7[5]),
    .d3(multiplexer_7_out[4]), .q3(D_q7[4]), .d4(multiplexer_7_out[3]), .q4(D_q7[3]),
    .d5(multiplexer_7_out[2]), .q5(D_q7[2]), .d6(multiplexer_7_out[1]), .q6(D_q7[1]),
    .d7(multiplexer_7_out[0]), .q7(D_q7[0]));  // open: in, out, clr
  and and_12 (and_12_out[0], or_3_out, not_1_out);
  and and_13 (and_12_out[1], not_1_out, or_4_out);
  and and_14 (and_12_out[2], not_1_out, decoder_3_out27);
  Shift_Register H (
    .shift(1'b0), .clk(clock_1_out), .load(or_4_out), .d0(HL_LOAD_h_2[7]), .q0(H_q7[7]), .d1(HL_LOAD_h_2[6]),
    .q1(H_q7[6]), .d2(HL_LOAD_h_2[5]), .q2(H_q7[5]), .d3(HL_LOAD_h_2[4]), .q3(H_q7[4]), .d4(HL_LOAD_h_2[3]),
    .q4(H_q7[3]), .d5(HL_LOAD_h_2[2]), .q5(H_q7[2]), .d6(HL_LOAD_h_2[1]), .q6(H_q7[1]), .d7(HL_LOAD_h_2[0]),
    .q7(H_q7[0]));  // open: in, out, clr
  or or_17 (or_17_out, decoder_2_out2, decoder_3_out15);
  or or_18 (or_18_out, decoder_2_out3[0], decoder_2_out3[1], decoder_2_out5);
  Shift_Register #(.length(16)) PC (
    .shift(1'b0), .clk(clock_1_out), .load(or_17_out), .d0(multiplexer_9_out[15]), .q0(PC_q15[15]),
    .d1(multiplexer_9_out[14]), .q1(PC_q15[14]), .d2(multiplexer_9_out[13]), .q2(PC_q15[13]),
    .d3(multiplexer_9_out[12]), .q3(PC_q15[12]), .d4(multiplexer_9_out[11]), .q4(PC_q15[11]),
    .d5(multiplexer_9_out[10]), .q5(PC_q15[10]), .d6(multiplexer_9_out[9]), .q6(PC_q15[9]),
    .d7(multiplexer_9_out[8]), .q7(PC_q15[8]), .d8(multiplexer_9_out[7]), .q8(PC_q15[7]),
    .d9(multiplexer_9_out[6]), .q9(PC_q15[6]), .d10(multiplexer_9_out[5]), .q10(PC_q15[5]),
    .d11(multiplexer_9_out[4]), .q11(PC_q15[4]), .d12(multiplexer_9_out[3]), .q12(PC_q15[3]),
    .d13(multiplexer_9_out[2]), .q13(PC_q15[2]), .d14(multiplexer_9_out[1]), .q14(PC_q15[1]),
    .d15(multiplexer_9_out[0]), .q15(PC_q15[0]));  // open: in, out, clr
  Shift_Register #(.length(16)) SP (
    .shift(1'b0), .clk(clock_1_out), .load(or_18_out), .d0(multiplexer_10_out[15]), .q0(SP_q15[15]),
    .d1(multiplexer_10_out[14]), .q1(SP_q15[14]), .d2(multiplexer_10_out[13]), .q2(SP_q15[13]),
    .d3(multiplexer_10_out[12]), .q3(SP_q15[12]), .d4(multiplexer_10_out[11]), .q4(SP_q15[11]),
    .d5(multiplexer_10_out[10]), .q5(SP_q15[10]), .d6(multiplexer_10_out[9]), .q6(SP_q15[9]),
    .d7(multiplexer_10_out[8]), .q7(SP_q15[8]), .d8(multiplexer_10_out[7]), .q8(SP_q15[7]),
    .d9(multiplexer_10_out[6]), .q9(SP_q15[6]), .d10(multiplexer_10_out[5]), .q10(SP_q15[5]),
    .d11(multiplexer_10_out[4]), .q11(SP_q15[4]), .d12(multiplexer_10_out[3]), .q12(SP_q15[3]),
    .d13(multiplexer_10_out[2]), .q13(SP_q15[2]), .d14(multiplexer_10_out[1]), .q14(SP_q15[1]),
    .d15(multiplexer_10_out[0]), .q15(SP_q15[0]));  // open: in, out, clr
  Clock clock_1 (.out(clock_1_out));
  Multiplexer #(.width(16), .enable("false")) multiplexer_9 (
    .in0(adder_3_out), .in1({D_q7, E_q7}), .out(multiplexer_9_out), .sel(decoder_3_out15));
  Multiplexer #(.select(2), .width(16), .enable("false")) multiplexer_10 (
    .in0({H_q7, L_q7}), .in1(adder_4_out), .in2(subtractor_3_out), .out(multiplexer_10_out),
    .sel(decoder_2_out3));  // open: in3
  RAM #(.addrWidth(16), .bus("separate")) ram_1 (
    .addr(multiplexer_8_out), .din(multiplexer_7_out), .data(ram_1_data), .str(or_7_out), .clk(clock_1_out),
    .ld(1'b1));  // open: sel, clr
  Shift_Register C (
    .shift(1'b0), .clk(clock_1_out), .load(or_6_out), .d0(multiplexer_7_out[7]), .q0(C_q7[7]),
    .d1(multiplexer_7_out[6]), .q1(C_q7[6]), .d2(multiplexer_7_out[5]), .q2(C_q7[5]),
    .d3(multiplexer_7_out[4]), .q3(C_q7[4]), .d4(multiplexer_7_out[3]), .q4(C_q7[3]),
    .d5(multiplexer_7_out[2]), .q5(C_q7[2]), .d6(multiplexer_7_out[1]), .q6(C_q7[1]),
    .d7(multiplexer_7_out[0]), .q7(C_q7[0]));  // open: in, out, clr
  Shift_Register E (
    .shift(1'b0), .clk(clock_1_out), .load(or_9_out), .d0(multiplexer_7_out[7]), .q0(E_q7[7]),
    .d1(multiplexer_7_out[6]), .q1(E_q7[6]), .d2(multiplexer_7_out[5]), .q2(E_q7[5]),
    .d3(multiplexer_7_out[4]), .q3(E_q7[4]), .d4(multiplexer_7_out[3]), .q4(E_q7[3]),
    .d5(multiplexer_7_out[2]), .q5(E_q7[2]), .d6(multiplexer_7_out[1]), .q6(E_q7[1]),
    .d7(multiplexer_7_out[0]), .q7(E_q7[0]));  // open: in, out, clr
  HL_LOAD_LOGIC HL_LOAD (
    .SELECT(and_12_out), .PC(PC_q15), .BUS(multiplexer_7_out), .H_2(HL_LOAD_h_2), .L_2(HL_LOAD_l_2),
    .H(H_q7), .L(L_q7), .DE({D_q7, E_q7}));
  Shift_Register L (
    .shift(1'b0), .clk(clock_1_out), .load(or_3_out), .d0(HL_LOAD_l_2[7]), .q0(L_q7[7]), .d1(HL_LOAD_l_2[6]),
    .q1(L_q7[6]), .d2(HL_LOAD_l_2[5]), .q2(L_q7[5]), .d3(HL_LOAD_l_2[4]), .q3(L_q7[4]), .d4(HL_LOAD_l_2[3]),
    .q4(L_q7[3]), .d5(HL_LOAD_l_2[2]), .q5(L_q7[2]), .d6(HL_LOAD_l_2[1]), .q6(L_q7[1]), .d7(HL_LOAD_l_2[0]),
    .q7(L_q7[0]));  // open: in, out, clr
  Adder #(.width(16)) adder_3 (.a(16'h1), .b(PC_q15), .out(adder_3_out));  // open: cin, cout
  Adder #(.width(16)) adder_4 (.a(16'h1), .b(SP_q15), .out(adder_4_out));  // open: cin, cout
  Subtractor #(.width(16)) subtractor_3 (.a(SP_q15), .b(16'h1), .out(subtractor_3_out));  // open: bin, bout
  or or_19 (or_19_out, decoder_3_out3, F_q1[1], decoder_3_out5);
  ALS als_1 (
    .BUS(multiplexer_7_out), .AC(AC_q7), .CIN(or_19_out), .OUTPUT(als_1_output),
    .CARRY_BORROW(als_1_carry_borrow), .SELECT_OPERATION(or_25_out));
  Shift_Register AC (
    .shift(1'b0), .clk(clock_1_out), .load(or_2_out), .d0(multiplexer_11_out[7]), .q0(AC_q7[7]),
    .d1(multiplexer_11_out[6]), .q1(AC_q7[6]), .d2(multiplexer_11_out[5]), .q2(AC_q7[5]),
    .d3(multiplexer_11_out[4]), .q3(AC_q7[4]), .d4(multiplexer_11_out[3]), .q4(AC_q7[3]),
    .d5(multiplexer_11_out[2]), .q5(AC_q7[2]), .d6(multiplexer_11_out[1]), .q6(AC_q7[1]),
    .d7(multiplexer_11_out[0]), .q7(AC_q7[0]));  // open: in, out, clr
  Shift_Register TEMP (
    .shift(1'b0), .clk(clock_1_out), .load(decoder_2_out8), .d0(AC_q7[7]), .q0(TEMP_q7[7]), .d1(AC_q7[6]),
    .q1(TEMP_q7[6]), .d2(AC_q7[5]), .q2(TEMP_q7[5]), .d3(AC_q7[4]), .q3(TEMP_q7[4]), .d4(AC_q7[3]),
    .q4(TEMP_q7[3]), .d5(AC_q7[2]), .q5(TEMP_q7[2]), .d6(AC_q7[1]), .q6(TEMP_q7[1]), .d7(AC_q7[0]),
    .q7(TEMP_q7[0]));  // open: in, out, clr
  or or_20 (or_20_out[0], decoder_4_out2, decoder_4_out3, decoder_4_out4, decoder_4_out5, decoder_4_out6, decoder_4_out8, decoder_4_out9, decoder_4_out10, decoder_4_out9, decoder_4_out12, decoder_4_out6, decoder_4_out5, decoder_4_out7);
  or or_21 (or_21_out, or_20_out[1], or_20_out[0]);
  Multiplexer #(.width(8), .enable("false")) multiplexer_11 (
    .in0(als_1_output), .in1(TEMP_q7), .out(multiplexer_11_out), .sel(decoder_2_out7));
  or or_22 (or_25_out[3], decoder_2_out10, decoder_4_out6, decoder_4_out12, decoder_4_out9);
  Decoder #(.select(5), .enable("false")) decoder_4 (
    .out2(decoder_4_out2), .out3(decoder_4_out3), .out4(decoder_4_out4), .out5(decoder_4_out5),
    .out6(decoder_4_out6), .out7(decoder_4_out7), .out8(decoder_4_out8), .out9(decoder_4_out9),
    .out10(decoder_4_out10), .out11(decoder_4_out9), .out12(decoder_4_out12), .out13(decoder_4_out6),
    .out14(decoder_4_out5), .sel(F2));  // open: out0, out1, out15, out16, out17, out18, out19, out20, out21, out22, out23, out24, out25, out26, out27, out28, out29, out30, out31
  or or_23 (or_25_out[2], decoder_4_out5, decoder_4_out10, decoder_4_out9, decoder_4_out8, decoder_4_out7);
  or or_24 (or_25_out[1], decoder_4_out12, decoder_4_out10, decoder_4_out9, decoder_4_out6, decoder_4_out6, decoder_4_out5, decoder_4_out4);
  Multiplexer #(.enable("false")) multiplexer_12 (
    .in0(F_q1[3]), .in1(flag_processor_1_s), .out(multiplexer_12_out), .sel(or_20_out[0]));
  Multiplexer #(.enable("false")) multiplexer_13 (
    .in0(F_q1[0]), .in1(flag_processor_1_z), .out(multiplexer_13_out), .sel(or_20_out[0]));
  Shift_Register F (
    .shift(1'b0), .clk(clock_1_out), .load(or_21_out), .d0(multiplexer_12_out), .q0(F_q1[3]),
    .d1(multiplexer_13_out), .q1(F_q1[0]), .d2(1'b0), .d3(multiplexer_15_out), .q3(F_q3), .d4(1'b0),
    .d5(multiplexer_14_out), .q5(F_q1[2]), .d6(1'b1), .d7(multiplexer_16_out), .q7(F_q1[1]));  // open: in, out, clr, q2, q4, q6
  Multiplexer #(.enable("false")) multiplexer_14 (
    .in0(F_q1[2]), .in1(flag_processor_1_p), .out(multiplexer_14_out), .sel(or_20_out[0]));
  Multiplexer #(.enable("false")) multiplexer_15 (.in0(F_q3), .in1(1'b0), .out(multiplexer_15_out), .sel(1'b0));
  FLAG_PROCESSOR flag_processor_1 (
    .ALS(als_1_output), .CIN(als_1_carry_borrow), .CY(flag_processor_1_cy), .P(flag_processor_1_p),
    .Z(flag_processor_1_z), .S(flag_processor_1_s));
  or or_25 (or_25_out[0], decoder_4_out6, decoder_4_out9, decoder_4_out9, decoder_4_out8, decoder_4_out6, decoder_4_out3, decoder_4_out2);
  Multiplexer #(.select(2), .enable("false")) multiplexer_16 (
    .in0(F_q1[1]), .in1(flag_processor_1_cy), .in2(not_6_out), .in3(not_6_out), .out(multiplexer_16_out),
    .sel(or_20_out));
  not not_2 (not_2_out, F_q1[0]);
  not not_3 (not_3_out, F_q1[1]);
  not not_4 (not_4_out, F_q1[2]);
  Multiplexer #(.select(3), .enable("false")) multiplexer_17 (
    .in0(not_2_out), .in1(F_q1[0]), .in2(not_3_out), .in3(F_q1[1]), .in4(not_4_out), .in5(F_q1[2]),
    .in6(not_5_out), .in7(F_q1[3]), .out(multiplexer_17_out), .sel(B_q4));
  not not_5 (not_5_out, F_q1[3]);
  not not_6 (not_6_out, F_q1[1]);
  not not_7 (not_7_out, 1'b1);
  Multiplexer #(.enable("false")) multiplexer_18 (
    .in0(1'b1), .in1(multiplexer_17_out), .out(multiplexer_18_out), .sel(rom_1_data_3[11]));
  Multiplexer #(.select(2), .enable("false")) multiplexer_19 (
    .in0(1'b1), .in1(1'b1), .in2(not_7_out), .in3(1'b1), .out(multiplexer_19_out), .sel(rom_1_data));
  Multiplexer #(.select(2), .enable("false")) multiplexer_20 (
    .in0(not_7_out), .in1(not_7_out), .in2(1'b1), .in3(1'b1), .out(multiplexer_20_out), .sel(rom_1_data));
  and and_15 (and_16_out[1], multiplexer_19_out, multiplexer_18_out);
  and and_16 (and_16_out[0], multiplexer_18_out, multiplexer_20_out);
  not not_8 (not_8_out, rom_1_data[1]);
  and and_17 (and_17_out, not_8_out, rom_1_data[0], multiplexer_18_out);
  MAPPING_LOGIC mapping_logic_1 (.INPUT({B_q1, B_q4, B_q7}), .OUTPUT(mapping_logic_1_output));
  Shift_Register #(.length(9)) CAR (
    .shift(1'b0), .clk(clock_1_out), .load(1'b1), .d0(multiplexer_21_out[8]), .q0(CAR_q8[8]),
    .d1(multiplexer_21_out[7]), .q1(CAR_q8[7]), .d2(multiplexer_21_out[6]), .q2(CAR_q8[6]),
    .d3(multiplexer_21_out[5]), .q3(CAR_q8[5]), .d4(multiplexer_21_out[4]), .q4(CAR_q8[4]),
    .d5(multiplexer_21_out[3]), .q5(CAR_q8[3]), .d6(multiplexer_21_out[2]), .q6(CAR_q8[2]),
    .d7(multiplexer_21_out[1]), .q7(CAR_q8[1]), .d8(multiplexer_21_out[0]), .q8(CAR_q8[0]));  // open: in, out, clr
  Multiplexer #(.select(2), .width(9), .enable("false")) multiplexer_21 (
    .in0(adder_5_out), .in1(SBR_q8), .in2(rom_1_data_2), .in3(mapping_logic_1_output),
    .out(multiplexer_21_out), .sel(and_16_out));
  ROM #(.addrWidth(9), .dataWidth(22)) rom_1 (
    .addr(CAR_q8), .data({f0, F1, F2, rom_1_data_3[11], rom_1_data, rom_1_data_2}));  // open: sel
  Adder #(.width(9)) adder_5 (.a(9'h1), .b(CAR_q8), .out(adder_5_out));  // open: cin, cout
  Shift_Register #(.length(9)) SBR (
    .shift(1'b0), .clk(clock_1_out), .load(and_17_out), .d0(adder_5_out[8]), .q0(SBR_q8[8]),
    .d1(adder_5_out[7]), .q1(SBR_q8[7]), .d2(adder_5_out[6]), .q2(SBR_q8[6]), .d3(adder_5_out[5]),
    .q3(SBR_q8[5]), .d4(adder_5_out[4]), .q4(SBR_q8[4]), .d5(adder_5_out[3]), .q5(SBR_q8[3]),
    .d6(adder_5_out[2]), .q6(SBR_q8[2]), .d7(adder_5_out[1]), .q7(SBR_q8[1]), .d8(adder_5_out[0]),
    .q8(SBR_q8[0]));  // open: in, out, clr

  // Notes on the sheet:
  //   DECODING R
  //   EF1OP2
  //   EF2OP1
  //   CY
  //   P
  //   S
  //   Z
  //   AC
  //   OPERATION SELECT FOR ALS
  //   CY   P   AC   Z   S
  //   TEST LOGIC
  //   BRANCH LOGIC
  //   SBR LOAD LOGIC
  //   contents of rom_1 (hex, n*v repeats v):
  //   198 6*0 1 20009 25500a 2000b 55198 0 0 1 1 8*0 19019 21a01a 58198 13*0 19029 21a02a 58198 21*0 20041
  //   1ba042 59043 1a0044 40198 0 0 0 2039c 1e004a 58198 5*0 2039c 1e0052 54198 37*0 20079 55198 70*0 1198
  //   15*0 2198 199*0 20199 5019a 600 0 5319d 2019e 12400
endmodule

module ALS (
  input  CIN,
  input  [7:0] BUS,
  input  [7:0] AC,
  input  [3:0] SELECT_OPERATION,
  output [7:0] OUTPUT,
  output CARRY_BORROW
);

  wire adder_1_cout, adder_2_cout, subtractor_1_bout, subtractor_2_bout;
  wire [7:0] adder_1_out, adder_2_out, and_1_out, not_1_out, or_1_out, subtractor_1_out, subtractor_2_out,
       xor_1_out;

  Adder adder_1 (.a(BUS), .b(AC), .out(adder_1_out), .cin(CIN), .cout(adder_1_cout));
  Subtractor subtractor_1 (.a(AC), .b(BUS), .out(subtractor_1_out), .bin(CIN), .bout(subtractor_1_bout));
  Adder adder_2 (.a(BUS), .b(8'h1), .out(adder_2_out), .cout(adder_2_cout));  // open: cin
  Subtractor subtractor_2 (.a(BUS), .b({8{1'b0}}), .out(subtractor_2_out), .bin(1'b1), .bout(subtractor_2_bout));
  assign and_1_out = BUS & AC;  // AND_Gate and_1, 8 bits wide
  assign or_1_out = BUS | AC;  // OR_Gate or_1, 8 bits wide
  assign xor_1_out = BUS ^ AC;  // XOR_Gate xor_1, 8 bits wide
  assign not_1_out = ~AC;  // NOT_Gate not_1, 8 bits wide
  Multiplexer #(.select(4), .width(8), .enable("false")) multiplexer_1 (
    .in0(BUS), .in1(adder_1_out), .in2(subtractor_1_out), .in3(adder_2_out), .in4(subtractor_2_out),
    .in5(and_1_out), .in6(or_1_out), .in7(xor_1_out), .in8(not_1_out), .in9({AC[6:0], AC[7]}),
    .in10({AC[0], AC[7:1]}), .in11({AC[6:0], CIN}), .in12({CIN, AC[7:1]}), .out(OUTPUT),
    .sel(SELECT_OPERATION));  // open: in13, in14, in15
  Multiplexer #(.select(4), .enable("false")) multiplexer_2 (
    .in0(1'b0), .in1(adder_1_cout), .in2(subtractor_1_bout), .in3(adder_2_cout), .in4(subtractor_2_bout),
    .in5(1'b0), .in6(1'b0), .in7(1'b0), .in8(1'b0), .in9(AC[7]), .in10(AC[0]), .in11(AC[7]), .in12(AC[0]),
    .out(CARRY_BORROW), .sel(SELECT_OPERATION));  // open: in13, in14, in15

  // Notes on the sheet:
  //   TRANSFER
  //   ADDER
  //   SUBTRACTOR
  //   INCREMENTOR
  //   DECREMENTOR
  //   AND
  //   OR
  //   XOR
  //   NOT
  //   RLC
  //   RRC
  //   RAL
  //   RAR
endmodule

module FLAG_PROCESSOR (
  input  [7:0] ALS,
  input  CIN,
  output CY,
  output P,
  output Z,
  output S
);

  wire or_1_out, or_2_out, or_3_out, or_4_out, or_5_out, or_6_out, xor_1_out, xor_2_out, xor_3_out,
       xor_4_out, xor_5_out, xor_6_out;

  xor xor_1 (xor_1_out, ALS[0], ALS[1]);
  or or_1 (or_1_out, ALS[0], ALS[1]);
  xor xor_2 (xor_2_out, xor_1_out, ALS[2]);
  or or_2 (or_2_out, or_1_out, ALS[2]);
  or or_3 (or_3_out, or_2_out, ALS[3]);
  xor xor_3 (xor_3_out, xor_2_out, ALS[3]);
  xor xor_4 (xor_4_out, xor_3_out, ALS[4]);
  or or_4 (or_4_out, or_3_out, ALS[4]);
  or or_5 (or_5_out, or_4_out, ALS[5]);
  xor xor_5 (xor_5_out, xor_4_out, ALS[5]);
  or or_6 (or_6_out, or_5_out, ALS[6]);
  or or_7 (Z, or_6_out, ALS[7]);
  xor xor_6 (xor_6_out, xor_5_out, ALS[6]);
  xor xor_7 (P, xor_6_out, ALS[7]);

  assign CY = CIN;
  assign S = ALS[7];
endmodule

module HL_LOAD_LOGIC (
  input  [15:0] DE,
  input  [15:0] PC,
  input  [7:0] BUS,
  input  [2:0] SELECT,
  input  [7:0] H,
  input  [7:0] L,
  output [7:0] H_2,
  output [7:0] L_2
);

  wire adder_2_cout;
  wire [7:0] adder_1_out, adder_2_out;

  Multiplexer #(.select(3), .width(8), .enable("false")) multiplexer_1 (
    .in0(DE[15:8]), .in1(H), .in2(BUS), .in3(PC[15:8]), .in4(adder_1_out), .out(H_2), .sel(SELECT));  // open: in5, in6, in7
  Multiplexer #(.select(3), .width(8), .enable("false")) multiplexer_2 (
    .in0(DE[7:0]), .in1(BUS), .in2(L), .in3(PC[7:0]), .in4(adder_2_out), .out(L_2), .sel(SELECT));  // open: in5, in6, in7
  Adder adder_1 (.a(H), .b({8{1'b0}}), .out(adder_1_out), .cin(adder_2_cout));  // open: cout
  Adder adder_2 (.a(L), .b(8'h1), .out(adder_2_out), .cout(adder_2_cout));  // open: cin

  // Notes on the sheet:
  //   NEXT STATE
  //   PREVIOUS STATE
  //   0 0  0 HL<-DE
  //   0 0 1  LOAD L
  //   0 1 0  LOAD H
  //   0 1 1  HL<-PC
  //   1 0 0  HL<-HL+1
endmodule

module CONTROL_BLOCK (
  input  [7:0] MEMORY_WORD,
  input  CLOCK,
  input  Z,
  input  CY,
  input  P,
  input  S,
  output f0,
  output [3:0] F1,
  output [4:0] F2
);

  wire and_3_out, multiplexer_1_out, multiplexer_2_out, multiplexer_3_out, multiplexer_4_out, not_1_out,
       not_2_out, not_3_out, not_4_out, not_5_out, not_6_out;
  wire [1:0] and_2_out;
  wire [8:0] adder_1_out, CAR_q8, mapping_logic_1_output, multiplexer_5_out, SBR_q8;
  wire [11:0] rom_1_data;

  not not_1 (not_1_out, Z);
  not not_2 (not_2_out, CY);
  not not_3 (not_3_out, P);
  not not_4 (not_4_out, S);
  Multiplexer #(.select(3), .enable("false")) multiplexer_1 (
    .in0(not_1_out), .in1(Z), .in2(not_2_out), .in3(CY), .in4(not_3_out), .in5(P), .in6(not_4_out), .in7(S),
    .out(multiplexer_1_out), .sel(MEMORY_WORD[5:3]));
  Multiplexer #(.enable("false")) multiplexer_2 (
    .in0(1'b1), .in1(multiplexer_1_out), .out(multiplexer_2_out), .sel(rom_1_data[11]));
  not not_5 (not_5_out, 1'b1);
  Multiplexer #(.select(2), .enable("false")) multiplexer_3 (
    .in0(1'b1), .in1(1'b1), .in2(not_5_out), .in3(1'b1), .out(multiplexer_3_out), .sel(rom_1_data[10:9]));
  Multiplexer #(.select(2), .enable("false")) multiplexer_4 (
    .in0(not_5_out), .in1(not_5_out), .in2(1'b1), .in3(1'b1), .out(multiplexer_4_out), .sel(rom_1_data[10:9]));
  and and_1 (and_2_out[1], multiplexer_3_out, multiplexer_2_out);
  and and_2 (and_2_out[0], multiplexer_2_out, multiplexer_4_out);
  not not_6 (not_6_out, rom_1_data[10]);
  MAPPING_LOGIC mapping_logic_1 (.INPUT(MEMORY_WORD), .OUTPUT(mapping_logic_1_output));
  and and_3 (and_3_out, not_6_out, rom_1_data[9], multiplexer_2_out);
  Shift_Register #(.length(9)) CAR (
    .shift(1'b0), .clk(CLOCK), .load(1'b1), .d0(multiplexer_5_out[8]), .q0(CAR_q8[8]),
    .d1(multiplexer_5_out[7]), .q1(CAR_q8[7]), .d2(multiplexer_5_out[6]), .q2(CAR_q8[6]),
    .d3(multiplexer_5_out[5]), .q3(CAR_q8[5]), .d4(multiplexer_5_out[4]), .q4(CAR_q8[4]),
    .d5(multiplexer_5_out[3]), .q5(CAR_q8[3]), .d6(multiplexer_5_out[2]), .q6(CAR_q8[2]),
    .d7(multiplexer_5_out[1]), .q7(CAR_q8[1]), .d8(multiplexer_5_out[0]), .q8(CAR_q8[0]));  // open: in, out, clr
  Multiplexer #(.select(2), .width(9), .enable("false")) multiplexer_5 (
    .in0(adder_1_out), .in1(SBR_q8), .in2(rom_1_data[8:0]), .in3(mapping_logic_1_output),
    .out(multiplexer_5_out), .sel(and_2_out));
  ROM #(.addrWidth(9), .dataWidth(22)) rom_1 (.addr(CAR_q8), .data({f0, F1, F2, rom_1_data}));  // open: sel
  Adder #(.width(9)) adder_1 (.a(9'h1), .b(CAR_q8), .out(adder_1_out));  // open: cin, cout
  Shift_Register #(.length(9)) SBR (
    .shift(1'b0), .clk(CLOCK), .load(and_3_out), .d0(adder_1_out[8]), .q0(SBR_q8[8]), .d1(adder_1_out[7]),
    .q1(SBR_q8[7]), .d2(adder_1_out[6]), .q2(SBR_q8[6]), .d3(adder_1_out[5]), .q3(SBR_q8[5]),
    .d4(adder_1_out[4]), .q4(SBR_q8[4]), .d5(adder_1_out[3]), .q5(SBR_q8[3]), .d6(adder_1_out[2]),
    .q6(SBR_q8[2]), .d7(adder_1_out[1]), .q7(SBR_q8[1]), .d8(adder_1_out[0]), .q8(SBR_q8[0]));  // open: in, out, clr

  // Notes on the sheet:
  //   TEST LOGIC
  //   BRANCH LOGIC
  //   SBR LOAD LOGIC
  //   contents of rom_1 (hex, n*v repeats v):
  //   198 6*0 1 6*0 1 1 64*0 4039c 198 326*0 20199 50600 0 0 5319d 2019e 12400
endmodule

module MAPPING_LOGIC (
  input  [7:0] INPUT,
  output [8:0] OUTPUT
);

  wire decoder_6_out0, decoder_6_out1, decoder_6_out2, decoder_6_out3, decoder_6_out4, decoder_6_out5,
       decoder_6_out7, decoder_10_out0, decoder_10_out1, decoder_10_out2, decoder_10_out3, decoder_13_out0,
       decoder_13_out1, decoder_13_out2, decoder_13_out3;
  wire [1:0] and_6_out, decoder_1_out1, decoder_3_out1, or_1_out;
  wire [1:1] decoder_4_out1, decoder_4_out3, decoder_8_out1;
  wire [4:0] and_8_out, and_10_out, and_11_out, decoder_10_out7, decoder_13_out7, priority_encoder_1_p1,
       priority_encoder_2_p17;
  wire [4:4] decoder_11_out1, decoder_11_out5, priority_encoder_1_p2;
  wire [7:0] and_2_out, and_7_out, and_9_out, decoder_2_out7, decoder_5_out7, decoder_7_out7, decoder_9_out7,
       decoder_12_out7;
  wire [7:7] decoder_4_out2, decoder_4_out7, decoder_6_out6, decoder_8_out2, decoder_11_out3;
  wire [21:0] decoder_11_out7, priority_encoder_2_p26;
  wire [21:21] decoder_8_out3;
  wire [23:0] and_4_out, decoder_4_out6;
  wire [23:23] decoder_8_out0;

  Decoder #(.enable("false")) decoder_1 (.out0(decoder_1_out1[1]), .out1(decoder_1_out1[0]), .sel(INPUT[3]));
  assign decoder_4_out6[22:21] = decoder_1_out1 & {2{decoder_4_out1[1]}};  // AND_Gate and_1, 2 bits wide
  assign and_2_out = {8{decoder_4_out2[7]}} & decoder_2_out7;  // AND_Gate and_2, 8 bits wide
  Decoder #(.select(3), .enable("false")) decoder_2 (
    .out0(decoder_2_out7[7]), .out1(decoder_2_out7[6]), .out2(decoder_2_out7[5]), .out3(decoder_2_out7[4]),
    .out4(decoder_2_out7[3]), .out5(decoder_2_out7[2]), .out6(decoder_2_out7[1]), .out7(decoder_2_out7[0]),
    .sel(INPUT[5:3]));
  Decoder #(.enable("false")) decoder_3 (.out0(decoder_3_out1[1]), .out1(decoder_3_out1[0]), .sel(INPUT[3]));
  assign decoder_4_out6[12:11] = decoder_3_out1 & {2{decoder_4_out3[1]}};  // AND_Gate and_3, 2 bits wide
  Decoder #(.select(3), .enable("false")) decoder_4 (
    .out0(decoder_4_out6[23]), .out1(decoder_4_out1[1]), .out2(decoder_4_out2[7]), .out3(decoder_4_out3[1]),
    .out4(decoder_4_out6[10]), .out5(decoder_4_out6[9]), .out6(decoder_4_out6[8]), .out7(decoder_4_out7[7]),
    .sel(INPUT[2:0]));
  assign and_4_out = {decoder_4_out6[23:21], and_2_out, decoder_4_out6[12:0]} & {24{decoder_8_out0[23]}};  // AND_Gate and_4, 24 bits wide
  Decoder #(.select(3), .enable("false")) decoder_5 (
    .out0(decoder_5_out7[7]), .out1(decoder_5_out7[6]), .out2(decoder_5_out7[5]), .out3(decoder_5_out7[4]),
    .out4(decoder_5_out7[3]), .out5(decoder_5_out7[2]), .out6(decoder_5_out7[1]), .out7(decoder_5_out7[0]),
    .sel(INPUT[5:3]));
  assign decoder_4_out6[7:0] = decoder_5_out7 & {8{decoder_4_out7[7]}};  // AND_Gate and_5, 8 bits wide
  or or_1 (or_1_out[1], decoder_6_out0, decoder_6_out1, decoder_6_out2, decoder_6_out3, decoder_6_out4, decoder_6_out5, decoder_6_out7, and_7_out[4], and_7_out[3], and_7_out[2], and_7_out[0], and_7_out[7], and_7_out[6], and_7_out[5]);
  assign and_6_out = or_1_out & {2{decoder_8_out1[1]}};  // AND_Gate and_6, 2 bits wide
  Decoder #(.select(3), .enable("false")) decoder_6 (
    .out0(decoder_6_out0), .out1(decoder_6_out1), .out2(decoder_6_out2), .out3(decoder_6_out3),
    .out4(decoder_6_out4), .out5(decoder_6_out5), .out6(decoder_6_out6[7]), .out7(decoder_6_out7),
    .sel(INPUT[2:0]));
  Decoder #(.select(3), .enable("false")) decoder_7 (
    .out0(decoder_7_out7[7]), .out1(decoder_7_out7[6]), .out2(decoder_7_out7[5]), .out3(decoder_7_out7[4]),
    .out4(decoder_7_out7[3]), .out5(decoder_7_out7[2]), .out6(decoder_7_out7[1]), .out7(decoder_7_out7[0]),
    .sel(INPUT[5:3]));
  assign {and_7_out[7:2], or_1_out[0], and_7_out[0]} = decoder_7_out7 & {8{decoder_6_out6[7]}};  // AND_Gate and_7, 8 bits wide
  // Priority_Encoder #(.select(5)) priority_encoder_1: pin names not known; wires that end beside it: priority_encoder_1_p1, priority_encoder_1_p2[4], and_9_out[7], and_9_out[6], and_9_out[5], and_9_out[4], and_9_out[3], and_9_out[2], OUTPUT[8]
  assign and_8_out = priority_encoder_1_p1 & {5{priority_encoder_1_p2[4]}};  // AND_Gate and_8, 5 bits wide
  Decoder #(.select(2), .enable("false")) decoder_8 (
    .out0(decoder_8_out0[23]), .out1(decoder_8_out1[1]), .out2(decoder_8_out2[7]), .out3(decoder_8_out3[21]),
    .sel(INPUT[7:6]));
  assign OUTPUT[7:3] = and_8_out | and_10_out;  // OR_Gate or_2, 5 bits wide
  assign and_9_out = {8{decoder_8_out2[7]}} & decoder_9_out7;  // AND_Gate and_9, 8 bits wide
  Decoder #(.select(3), .enable("false")) decoder_9 (
    .out0(decoder_9_out7[7]), .out1(decoder_9_out7[6]), .out2(decoder_9_out7[5]), .out3(decoder_9_out7[4]),
    .out4(decoder_9_out7[3]), .out5(decoder_9_out7[2]), .out6(decoder_9_out7[1]), .out7(decoder_9_out7[0]),
    .sel(INPUT[5:3]));
  // Priority_Encoder #(.select(5)) priority_encoder_2: pin names not known; wires that end beside it: and_9_out[1], and_9_out[0], priority_encoder_2_p26[21], priority_encoder_2_p26[20], priority_encoder_2_p26[19], priority_encoder_2_p26[18], priority_encoder_2_p26[17], priority_encoder_2_p26[16], priority_encoder_2_p26[15], priority_encoder_2_p26[14], priority_encoder_2_p26[13], priority_encoder_2_p26[12], priority_encoder_2_p26[11], priority_encoder_2_p26[10], priority_encoder_2_p26[9], priority_encoder_2_p26[8], priority_encoder_2_p17, priority_encoder_2_p26[7], OUTPUT[8], priority_encoder_2_p26[6], priority_encoder_2_p26[5], priority_encoder_2_p26[4], priority_encoder_2_p26[3], priority_encoder_2_p26[2], priority_encoder_2_p26[1], priority_encoder_2_p26[0]
  assign and_10_out = priority_encoder_2_p17 & {5{OUTPUT[8]}};  // AND_Gate and_10, 5 bits wide
  Decoder #(.select(3), .enable("false")) decoder_10 (
    .out0(decoder_10_out0), .out1(decoder_10_out1), .out2(decoder_10_out2), .out3(decoder_10_out3),
    .out4(decoder_10_out7[3]), .out5(decoder_10_out7[2]), .out6(decoder_10_out7[1]),
    .out7(decoder_10_out7[0]), .sel(INPUT[5:3]));
  or or_3 (decoder_10_out7[4], decoder_10_out0, decoder_10_out1, decoder_10_out2, decoder_10_out3);
  assign and_11_out = decoder_10_out7 & {5{decoder_11_out1[4]}};  // AND_Gate and_11, 5 bits wide
  Decoder #(.select(3), .enable("false")) decoder_11 (
    .out0(decoder_11_out7[21]), .out1(decoder_11_out1[4]), .out2(decoder_11_out7[15]),
    .out3(decoder_11_out3[7]), .out4(decoder_11_out7[6]), .out5(decoder_11_out5[4]),
    .out7(decoder_11_out7[0]), .sel(INPUT[2:0]));  // open: out6
  Decoder #(.select(3), .enable("false")) decoder_12 (
    .out0(decoder_12_out7[7]), .out1(decoder_12_out7[6]), .out2(decoder_12_out7[5]),
    .out3(decoder_12_out7[4]), .out4(decoder_12_out7[3]), .out5(decoder_12_out7[2]),
    .out6(decoder_12_out7[1]), .out7(decoder_12_out7[0]), .sel(INPUT[5:3]));
  assign decoder_11_out7[14:7] = decoder_12_out7 & {8{decoder_11_out3[7]}};  // AND_Gate and_12, 8 bits wide
  Decoder #(.select(3), .enable("false")) decoder_13 (
    .out0(decoder_13_out0), .out1(decoder_13_out1), .out2(decoder_13_out2), .out3(decoder_13_out3),
    .out4(decoder_13_out7[3]), .out5(decoder_13_out7[2]), .out6(decoder_13_out7[1]),
    .out7(decoder_13_out7[0]), .sel(INPUT[5:3]));
  or or_4 (decoder_13_out7[4], decoder_13_out0, decoder_13_out1, decoder_13_out2, decoder_13_out3);
  assign decoder_11_out7[5:1] = decoder_13_out7 & {5{decoder_11_out5[4]}};  // AND_Gate and_13, 5 bits wide
  assign priority_encoder_2_p26 = {decoder_11_out7[21], and_11_out, decoder_11_out7[15:0]} & {22{decoder_8_out3[21]}};  // AND_Gate and_14, 22 bits wide

  assign OUTPUT[2:0] = 3'b000;
endmodule
